# Fritzing sketch ESP32_Wiring (saved by Fritzing 0.9.10b)
circuit board: 5.5cm x 5.5cm
breadboards: 1

parts:
  ESP32-CAM = ESP32 - CAM
  NEOPIXEL1 = Neopixel Strip -- Black (60/m) [part_number=1461]
  C1 = Electrolytic Capacitor [capacitance=1mF voltage=16V package="100 mil [THT, electrolytic]"]
  Boot = Momentary Switch [package=ksa_sealed_tac_switch]
  Level_Shifter = Adafruit 4-channel I2C-safe Bi-directional Logic Level Converter [part_number="Adafruit #757"]
  USBTTL1 = USB TTL Serial Cable
  USB_Power = USB Connectors [package=usb-b-pth-vertical]

nets:
  5V: ESP32-CAM.5V, NEOPIXEL1.+5V, C1.+, Level_Shifter.HV, USBTTL1.5V, USB_Power.VBUS
  GND: ESP32-CAM.GND, NEOPIXEL1.GND, C1.-, Boot.1, Level_Shifter.GND, USBTTL1.GND, USB_Power.GND
  N1: ESP32-CAM.IO13, Level_Shifter.A4
  N2: ESP32-CAM.VOT, USBTTL1.RX
  N3: ESP32-CAM.VOR, USBTTL1.TX
  N4: ESP32-CAM.IO0, Boot.3
  N5: ESP32-CAM.3V3, Level_Shifter.LV
  N6: NEOPIXEL1.DI, Level_Shifter.B4

custom parts:
  ESP32 - CAM: The ESP32-CAM has a very competitive small-size camera module that can operate independently as a minimum system with a footprint of only 27*40.5*4.5mm and a deep sleep current of up to 6mA.
  Neopixel Strip -- Black (60/m): Neopixel Strip, Black, 60 pixels per meter.
  Adafruit 4-channel I2C-safe Bi-directional Logic Level Converter: Because the Arduino (and Basic Stamp) are 5V devices, and most modern sensors, displays, flash cards and modes are 3.3V-only, many makers find that they need to perform level shifting/conversion to protect the 3.3V device from 5V. We do have some other handy level shifters in the shop, from the DIP 74LVC245 to the fancy bi-directional TXB0108. However, neither of these are happy to work with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
