# Fritzing sketch ESP32_Wiring_0.1 (saved by Fritzing 0.9.10b)
circuit board: 9.02299cm x 7.09735cm
breadboards: 1

parts:
  ESP32-CAM = ESP32 - CAM
  NEOPIXEL1 = Neopixel Strip -- Black (60/m) [part_number=1461]
  C1 = Electrolytic Capacitor [capacitance=1mF voltage=16V package="100 mil [THT, electrolytic]"]
  PROG = Momentary Switch [package=ksa_sealed_tac_switch]
  Level_Shifter = Adafruit 4-channel I2C-safe Bi-directional Logic Level Converter [part_number="Adafruit #757"]
  USBTTL1 = USB TTL Serial Cable
  USB/POWER = USB+SHIELD [package=usb-b-pth]
  J1 = female pin header, 4 pins [form="♀ (female)"]
  ^1_GPIO_Expansion = female pin header, 16 pins [form="♀ (female)"]
  Ground = female pin header, 4 pins [form="♀ (female)"]
  +5V = female pin header, 4 pins [form="♀ (female)"]
  AW9523_GPIO_Expansion = Adafruit AW9523 [part_number="Adafruit #4886"]

nets:
  5V: ESP32-CAM.5V, NEOPIXEL1.+5V, C1.+, Level_Shifter.HV, USBTTL1.5V, USB/POWER.VBUS, J1.pin2, +5V.pin1, +5V.pin2, +5V.pin3, +5V.pin4, AW9523_GPIO_Expansion.VCC
  GND: ESP32-CAM.GND, NEOPIXEL1.GND, C1.-, PROG.1, Level_Shifter.GND, USBTTL1.GND, USB/POWER.GND, J1.pin1, Ground.pin1, Ground.pin2, Ground.pin3, Ground.pin4, AW9523_GPIO_Expansion.GND
  N1: ESP32-CAM.IO13, Level_Shifter.A4
  N2: ESP32-CAM.VOT, USBTTL1.RX, J1.pin4
  N3: ESP32-CAM.VOR, USBTTL1.TX, J1.pin3
  N4: ESP32-CAM.IO0, PROG.3
  N5: ESP32-CAM.3V3, Level_Shifter.LV
  N6: NEOPIXEL1.DI, Level_Shifter.B4
  N7: ^1_GPIO_Expansion.pin1, AW9523_GPIO_Expansion.P0_0
  N8: ^1_GPIO_Expansion.pin2, AW9523_GPIO_Expansion.P0_1
  N9: ^1_GPIO_Expansion.pin3, AW9523_GPIO_Expansion.P0_2
  N10: ^1_GPIO_Expansion.pin4, AW9523_GPIO_Expansion.P0_3
  N11: ^1_GPIO_Expansion.pin5, AW9523_GPIO_Expansion.P0_4
  N12: ^1_GPIO_Expansion.pin6, AW9523_GPIO_Expansion.P0_5
  N13: ^1_GPIO_Expansion.pin7, AW9523_GPIO_Expansion.P0_6
  N14: ^1_GPIO_Expansion.pin8, AW9523_GPIO_Expansion.P0_7
  N15: ^1_GPIO_Expansion.pin9, AW9523_GPIO_Expansion.P1_0
  N16: ^1_GPIO_Expansion.pin10, AW9523_GPIO_Expansion.P1_1
  N17: ^1_GPIO_Expansion.pin11, ^1_GPIO_Expansion.pin13, AW9523_GPIO_Expansion.P1_2, AW9523_GPIO_Expansion.P1_4
  N18: ^1_GPIO_Expansion.pin12, AW9523_GPIO_Expansion.P1_3
  N19: ^1_GPIO_Expansion.pin14, AW9523_GPIO_Expansion.P1_5
  N20: ^1_GPIO_Expansion.pin15, AW9523_GPIO_Expansion.P1_6
  N21: ^1_GPIO_Expansion.pin16, AW9523_GPIO_Expansion.P1_7

notes:
  ZeBrAl
  ZeBrAl IoT 0.1

custom parts:
  ESP32 - CAM: The ESP32-CAM has a very competitive small-size camera module that can operate independently as a minimum system with a footprint of only 27*40.5*4.5mm and a deep sleep current of up to 6mA.
  Neopixel Strip -- Black (60/m): Neopixel Strip, Black, 60 pixels per meter.
  Adafruit 4-channel I2C-safe Bi-directional Logic Level Converter: Because the Arduino (and Basic Stamp) are 5V devices, and most modern sensors, displays, flash cards and modes are 3.3V-only, many makers find that they need to perform level shifting/conversion to protect the 3.3V device from 5V. We do have some other handy level shifters in the shop, from the DIP 74LVC245 to the fancy bi-directional TXB0108. However, neither of these are happy to work with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
  Adafruit AW9523: Expand your project possibilities, with the Adafruit AW9523 GPIO Expander and LED Driver Breakout - a cute and powerful I2C expander with a lot of tricks up it's sleeve. GPIO expanders work like this: you have a board with some number of GPIO but not enough for your project - maybe you need more buttons or LEDs. You could upgrade to a board with massive number of GPIO like the Grand Central,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
